// Logisim project Visto_2A.circ as structural Verilog: 1 circuit, main circuit main
module main (
  input  A,
  input  B,
  input  C,
  output out_4
);

  wire AB_out, AC_out, BC_out;

  and AB (AB_out, A, B);
  and AC (AC_out, A, C);
  and BC (BC_out, B, C);
  or or_1 (out_4, AB_out, AC_out, BC_out);

  // Notes on the sheet:
  //   T:
endmodule
