// Logisim project Visto_4.circ as structural Verilog: 1 circuit, main circuit main
module main (
  input  D0,
  input  S1,
  input  S0,
  input  D1,
  input  D2,
  input  D3,
  output out_7
);

  wire nand_1_out, nand_2_out, nand_3_out, nand_4_out, nand_5_out, nand_6_out;

  nand nand_1 (nand_1_out, S1, S1);
  nand nand_2 (nand_2_out, S0, S0);
  nand nand_3 (nand_3_out, D0, nand_1_out, nand_2_out);
  nand nand_4 (nand_4_out, D1, nand_1_out, S0);
  nand nand_5 (nand_5_out, D2, S1, nand_2_out);
  nand nand_6 (nand_6_out, D3, S1, S0);
  nand nand_7 (out_7, nand_3_out, nand_4_out, nand_5_out, nand_6_out);
endmodule
