// Logisim project Visto_2.circ as structural Verilog: 1 circuit, main circuit main
module main (
  input  A,
  input  B,
  input  C,
  input  D,
  input  E,
  input  F,
  input  G,
  output out_8
);

  wire decoder_1_out0, decoder_1_out9, decoder_1_out13, decoder_1_out14, decoder_1_out15, or_1_out, or_2_out;

  Decoder #(.select(4)) decoder_1 (
    .out0(decoder_1_out0), .out9(decoder_1_out9), .out13(decoder_1_out13), .out14(decoder_1_out14),
    .out15(decoder_1_out15), .sel({D, C, B, A}));  // open: out1, out2, out3, out4, out5, out6, out7, out8, out10, out11, out12, en
  or or_1 (or_1_out, decoder_1_out0, decoder_1_out15);
  or or_2 (or_2_out, decoder_1_out9, decoder_1_out15);
  Multiplexer #(.select(3), .enable("false")) multiplexer_1 (
    .in0(1'b0), .in1(or_2_out), .in2(decoder_1_out14), .in3(decoder_1_out13), .in4(or_1_out), .in5(1'b0),
    .in6(1'b1), .in7(1'b1), .out(out_8), .sel({G, F, E}));
endmodule
